// Logisim project cpu.circ as structural Verilog: 1 circuit, main circuit main
module main (
  input  [31:0] INSTRUCTION,
  input  CLOCK,
  output [31:0] PROGRAM_COUNTER,
  output [31:0] ra,
  output [31:0] sp,
  output [31:0] t0,
  output [31:0] t1,
  output [31:0] t2,
  output [31:0] s0,
  output [31:0] s1,
  output [31:0] a0,
  output [31:0] out_12,
  output [31:0] out_13,
  output [31:0] out_14
);

  wire ASel, BrEq, BrLt, BrUn, BSel, MemRW, PCSel, RegWEn;
  wire [1:0] WBSel;
  wire [2:0] funct3, ImmSel;
  wire [3:0] ALUSel;
  wire [6:0] imm;
  wire [24:0] INS_Q;
  wire [31:0] adder_1_out, ALU_inputA, ALU_inputB, DMEM_output, Inst, rs2_output;

  control_logic control_logic_1 (
    .BSel(BSel), .BrUn(BrUn), .RegWEn(RegWEn), .ImmSel(ImmSel), .ASel(ASel), .PCSel(PCSel), .BrLt(BrLt),
    .BrEq(BrEq), .inst(Inst), .ALUSel(ALUSel), .MemRW(MemRW), .WBSel(WBSel));
  Adder #(.width(32)) adder_1 (.a(PROGRAM_COUNTER), .b(32'h4), .out(adder_1_out));  // open: cin, cout
  Register #(.width(32)) PC (.D(adder_1_out), .clk(CLOCK), .Q(PROGRAM_COUNTER));  // open: en, clr
  Multiplexer #(.select(2), .width(32), .enable("false")) multiplexer_1 (
    .in1(out_13), .in2(DMEM_output), .out(out_14), .sel(WBSel));  // open: in0, in3
  // mem_main DMEM: pin names not known; wires that end beside it: out_14, CLOCK, MemRW, DMEM_output
  regfile_main RegFile (
    .rs2(INS_Q[24:20]), .rd(INS_Q[11:7]), .Read_Data_1(ALU_inputA), .Read_Data_2(rs2_output), .ra(ra),
    .sp(sp), .t0(t0), .t1(t1), .t2(t2), .s0(s0), .s1(s1), .a0(a0), .rs1(INS_Q[19:15]), .Write_Data(out_14),
    .RegWEn(RegWEn), .clk(CLOCK));
  imm_gen imm_gen_1 (.ImmSel(ImmSel), .inst({imm, INS_Q[24:15], funct3, INS_Q[11:0]}), .imm(out_12));
  Register #(.width(32)) register_1 (
    .D(INSTRUCTION), .clk(CLOCK), .Q({imm, INS_Q[24:15], funct3, INS_Q[11:0]}));  // open: en, clr
  Multiplexer #(.width(32), .enable("false")) multiplexer_2 (
    .in0(rs2_output), .in1(out_12), .out(ALU_inputB), .sel(BSel));
  alu Arithmetic_Logic_Unit (.ALUSel(ALUSel), .Result(out_13), .A(ALU_inputA), .B(ALU_inputB));
  // branch_comp branch_comp_1: pin names not known

  // Other names for the same wires on the sheet: ALU_output[31:0] = out_13; clk = CLOCK; ImmGen_output[31:0] = out_12;
  //   Opcode[6:0] = INS_Q[6:0]; rd_input[4:0] = INS_Q[11:7]; INS_Q (some bits) = {imm, funct3};
  //   rs1_input[4:0] = INS_Q[19:15]; rs2_input[4:0] = INS_Q[24:20]; rs1_output[31:0] = ALU_inputA;
  //   WB_output[31:0] = out_14

  // Notes on the sheet:
  //   Output
  //   IMEM (do **NOT** move this)
  //   Inputs
  //   It is OK to move the PC, RegFile, ALU, MEM, Branch Comp, Imm Gen, and Control Logic to wherever is most convenient for you when constructing your CPU, and to delete this text
  //   Inputs/Outputs for testing. Do **NOT** move these.
endmodule
